# Fritzing sketch MyVFD (saved by Fritzing 1.0.2b)

parts:
  R2 = Bussed8 Resistor-8 (SIP-9) [tolerance=±5% resistance=10k package=SIP-9]
  ULN1 = Darlington Driver [package=dil18]
  R4 = Resistor [tolerance=±5% power=0.25 resistance=100 package=THT]
  VFD1 = IC, SIP package, 19 pins [chip_label=9-ST-08A]
  R5 = Rotary Potentiometer (Small) [maximum_resistance=100Ω knob_status=50% power=0.5W package=THT]
  ULN2 = Darlington Driver [package=dil18]
  ULN3 = Darlington Driver [package=dil18]
  R6 = Resistor [tolerance=±5% power=0.25 resistance=10k package=THT]
  R1 = Bussed8 Resistor-8 (SIP-9) [tolerance=±5% resistance=10k package=SIP-9]
  M1 = DOIT Esp32 DevKit v1 (30 pins long, 11 pins width) [part_number=ESP32S-PIN30]
  Q1 = NPN-Transistor [package="TO92 [THT]"]
  R7 = Resistor [tolerance=±5% power=0.25 resistance=1k package=THT]
  R8 = Resistor [tolerance=±5% power=0.25 resistance=1k package=THT]
  IC2 = IC, DIP package, 8 pins [chip_label=TB67H450]

nets:
  30V: R2.Pin_0, VFD1.pin10, R6.Pin_1, R1.Pin_0
  N1: R2.Pin_1, VFD1.pin11, ULN2.17
  N2: R2.Pin_2, VFD1.pin12, ULN2.16
  N3: R2.Pin_3, VFD1.pin13, ULN2.15
  N4: R2.Pin_4, VFD1.pin14, ULN2.14
  N5: R2.Pin_5, VFD1.pin15, ULN2.13
  N6: R2.Pin_6, VFD1.pin16, ULN2.12
  N7: R2.Pin_7, VFD1.pin17, ULN2.11
  N8: R2.Pin_8, VFD1.pin18, ULN3.15
  N9: ULN1.2, M1.D15
  N10: ULN1.3, M1.D4
  N11: ULN1.4, M1.RX2
  N12: ULN1.5, M1.TX2
  N13: ULN1.6, M1.D18
  N14: ULN1.7, M1.D19
  N15: ULN1.8, M1.D21
  GND: ULN1.9, ULN2.9, ULN3.9, M1.GND, Q1.E, IC2.pin5
  N16: ULN1.11, VFD1.pin8, R1.Pin_2
  N17: ULN1.12, VFD1.pin7, R1.Pin_3
  N18: ULN1.13, VFD1.pin6, R1.Pin_4
  N19: ULN1.14, VFD1.pin5, R1.Pin_5
  N20: ULN1.15, VFD1.pin4, R1.Pin_6
  N21: ULN1.16, VFD1.pin3, R1.Pin_7
  N22: ULN1.17, VFD1.pin2, R1.Pin_8
  5V: R4.Pin_0, M1.VIN
  N23: R4.Pin_1, R5.leg2
  N24: VFD1.pin1, IC2.pin2
  N25: VFD1.pin9, ULN3.17, R1.Pin_1
  N26: VFD1.pin19, IC2.pin4
  N27: R5.wiper, IC2.pin1
  N28: ULN2.2, M1.D22
  N29: ULN2.3, M1.D23
  N30: ULN2.4, M1.D27
  N31: ULN2.5, M1.D26
  N32: ULN2.6, M1.D25
  N33: ULN2.7, M1.D33
  N34: ULN2.8, M1.D32
  N35: ULN3.2, M1.D13
  N36: ULN3.3, M1.D12
  N37: ULN3.4, M1.D14
  N38: ULN3.16, R6.Pin_0
  3.3V: M1.3V3, R8.Pin_0, IC2.pin8
  PWM: M1.D5, R7.Pin_0, IC2.pin6
  N39: Q1.B, R7.Pin_1
  N40: Q1.C, R8.Pin_1, IC2.pin7

notes:
  From DC-DC Convertor
  Invert PWM Signal

custom parts:
  Bussed8 Resistor-8 (SIP-9): A resistor array is a single package which contains more than one resistor. They are typically used for convenience when several resistors are needed together in the same place in a circuit.
  DOIT Esp32 DevKit v1 (30 pins long, 11 pins width): The DOIT Esp32 DevKit v1 is one of the development board created by DOIT to evaluate the ESP-WROOM-32 module. It is based on the ESP32 microcontroller that boasts Wifi, Bluetooth, Ethernet and Low Power support all in a single chip. (vanepp) made breadboard work, adjusted pin numbering and labels and reduced size of schematic and cleaned up pcb. This chip is 30pins long (2 x15) and 11 pins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
